# Fritzing sketch tinr2d2 (saved by Fritzing 0.8.7b)
perfboards: 1

parts:
  BTBeeV1 = XBee
  Propeller_QuickStart = Parallax Propeller D40 [package="DIP [THT]"]
  LED1 = LED - 3mm [color="Blue (525nm)" package="3 mm [THT]"]
  LED2 = LED - 3mm [color="Blue (525nm)" package="3 mm [THT]"]
  LED3 = LED - 3mm [color="Blue (525nm)" package="3 mm [THT]"]
  LED4 = LED - 3mm [color="Blue (525nm)" package="3 mm [THT]"]
  LED5 = LED - 3mm [color="Blue (525nm)" package="3 mm [THT]"]
  LED6 = LED - 3mm [color="Blue (525nm)" package="3 mm [THT]"]
  LED7 = LED - 3mm [color="Blue (525nm)" package="3 mm [THT]"]
  TB6612FNG = IC, DIP package, 16 pins [chip_label=IC]
  M1 = DC Motor
  M2 = DC Motor
  VM = 4 x AAA Battery Mount
  S7V8F3 = female pin header, 4 pins [form="♀ (female)"]
  VLOG = 4 x AAA Battery Mount
  MB1000 = female pin header, 7 pins [form="♀ (female)"]
  SPKR = Loudspeaker

nets:
  VCC/VOUT: BTBeeV1.VCC, TB6612FNG.pin2, TB6612FNG.pin13, S7V8F3.pin1, MB1000.pin2
  BT_TX: BTBeeV1.pin2, Propeller_QuickStart.P1
  BT_RX: BTBeeV1.pin3, Propeller_QuickStart.P0
  GND: BTBeeV1.GND, LED1.cathode, LED2.cathode, LED3.cathode, LED4.cathode, LED5.cathode, LED6.cathode, LED7.cathode, TB6612FNG.pin8, VM.+, S7V8F3.pin2, VLOG.+, MB1000.pin1, SPKR.pin2
  MOT_BIN1: Propeller_QuickStart.P2, TB6612FNG.pin12
  MOT_BIN2: Propeller_QuickStart.P3, TB6612FNG.pin11
  MOT_AIN2: Propeller_QuickStart.P4, TB6612FNG.pin15
  MOT_AIN1: Propeller_QuickStart.P5, TB6612FNG.pin14
  MOT_PWMA: Propeller_QuickStart.P6
  MOT_PWMB: Propeller_QuickStart.P7, TB6612FNG.pin10
  SPEAKER: Propeller_QuickStart.P8, SPKR.pin1
  USON_TX: Propeller_QuickStart.P9, MB1000.pin3
  P14: Propeller_QuickStart.P14, LED1.anode
  P16: Propeller_QuickStart.P16, LED5.anode
  P18: Propeller_QuickStart.P18, LED3.anode
  P20: Propeller_QuickStart.P20, LED7.anode
  P22: Propeller_QuickStart.P22, LED4.anode
  P24: Propeller_QuickStart.P24, LED2.anode
  P26: Propeller_QuickStart.P26, LED6.anode
  VM: TB6612FNG.pin1, VM.-
  N1: TB6612FNG.pin4, M1.pin_1
  N2: TB6612FNG.pin5, M1.pin_2
  N3: TB6612FNG.pin6, M2.pin_1
  N4: TB6612FNG.pin7, M2.pin_2
  VIN: S7V8F3.pin3, VLOG.-

notes:
  TinCanR2D2
